# Fritzing sketch arduino-client (saved by Fritzing 0.9.3b)
breadboards: 1

parts:
  Part1 = Arduino Uno (Rev3) - ICSP
  Part2 = Adafruit RFM9x LoRa Radio [part_number="Adafruit #3072 and #3073"]
  Part3 = Adafruit BME280

nets:
  N1: Part1.D10_PWM/SS, Part3.CS
  N2: Part1.D11_PWM/MOSI, Part2.MOSI, Part3.SDI/SDA
  N3: Part1.D12/MISO, Part2.MISO, Part3.SDO/ADR
  N4: Part1.D13/SCK, Part2.SCK, Part3.SCK/SCL
  N5: Part1.D2, Part2.RST
  N6: Part1.D3_PWM, Part2.DIO0
  N7: Part1.D4, Part2.CS
  VIN: Part1.5V, Part2.VIN, Part3.VIN
  GND: Part1.GND, Part2.GND, Part3.GND

custom parts:
  Adafruit RFM9x LoRa Radio: Sending data over long distances is like magic, and now you can be a magician with this range of powerful and easy-to-use radio modules. Sure, sometimes you want to talk to a computer (a good time to use WiFi) or perhaps communicate with a Phone (choose Bluetooth Low Energy!) but what if you want to send data very far? Most WiFi, Bluetooth, Zigbee and other wireless chipsets use 2.4GHz, which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
  Adafruit BME280: Bosch has stepped up their game with their new BME280 sensor, an environmental sensor with temperature, barometric pressure and humidity! This sensor is great for all sorts of weather/environmental sensing and can even be used in both I2C and SPI! This precision sensor from Bosch is the best low-cost sensing solution for measuring humidity with ±3% accuracy, barometric pressure with ±1 hPa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
