# Fritzing sketch rpi-server (saved by Fritzing 0.9.3b)
breadboards: 1

parts:
  Raspberry_Pi_1 = Raspberry Pi 3 [part_number=RPI-3-V1.2]
  Part1 = Adafruit RFM9x LoRa Radio [part_number="Adafruit #3072 and #3073"]

nets:
  3V3: Raspberry_Pi_1.3v3, Part1.VIN
  N1: Raspberry_Pi_1.GIPO10, Part1.MOSI
  N2: Raspberry_Pi_1.GIPO9, Part1.MISO
  N3: Raspberry_Pi_1.GIPO11, Part1.SCK
  N4: Raspberry_Pi_1.GIPO5, Part1.DIO0
  N5: Raspberry_Pi_1.GIPO7, Part1.CS
  N6: Raspberry_Pi_1.GIPO25, Part1.RST
  GND: Raspberry_Pi_1.GND, Part1.GND

custom parts:
  Adafruit RFM9x LoRa Radio: Sending data over long distances is like magic, and now you can be a magician with this range of powerful and easy-to-use radio modules. Sure, sometimes you want to talk to a computer (a good time to use WiFi) or perhaps communicate with a Phone (choose Bluetooth Low Energy!) but what if you want to send data very far? Most WiFi, Bluetooth, Zigbee and other wireless chipsets use 2.4GHz, which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
